# Fritzing sketch Untitled Sketch 2 (saved by Fritzing 0.9.3b)

parts:
  Часть1 = FTDI Basic Programmer
  Часть2 = Arduino Uno (Rev3) - ICSP

nets:
  N1: Часть1.RXI, Часть2.D1/TX
  N2: Часть1.TXO, Часть2.D0/RX
  N3: Часть1.POWER, Часть2.5V
  GND: Часть1.GND, Часть2.GND
